# Fritzing sketch electronics (saved by Fritzing 0.9.2b)
breadboards: 1

parts:
  IC1 = DS1307 [package=THT]
  R1 = Resistor [tolerance=±5% resistance=2.2k package=THT]
  R2 = Resistor [tolerance=±5% resistance=2.2k package=THT]
  U1 = SD_CARD_SOCKET [package=sdcard_4uconn]
  TFT1 = 1.8" TFT Display with uSD
  Atmega1 = ATmega644 [package=pdpi]
  C2 = Ceramic Capacitor [capacitance=10pF package="0805 [SMD, multilayer]"]
  C3 = Ceramic Capacitor [capacitance=100nF package="0805 [SMD, multilayer]"]
  C4 = Ceramic Capacitor [capacitance=10pF package="0805 [SMD, multilayer]"]
  XTAL1 = CRYSTAL - kHz [frequency="20 MHz"]
  XTAL2 = CRYSTAL - kHz [frequency="32 kHz"]
  KEYPAD1 = Membrane Matrix Keypad
  IC2 = Voltage Regulator [package=78xxl]
  BAT1 = Battery Holders [package=battcon_12mm_pth]
  BATT1 = 4xAA Switchable Battery Pack w/Bare Wire
  C5 = Electrolytic Capacitor [capacitance=10µF package="0807 [SMD, electrolytic]"]
  C6 = Electrolytic Capacitor [capacitance=10µF package="0807 [SMD, electrolytic]"]

nets:
  N1: IC1.X1_-_Crystal, XTAL2.pin_1
  N2: IC1.X2_-_Crystal, XTAL2.pin_0
  N3: IC1.Vbat_-_Backup_Supply, BAT1.+
  GND: IC1.0V, U1.SH, U1.VSS1, U1.VSS2, TFT1.BL, Atmega1.GND, C2.1, C3.1, C4.1, IC2.GND, BAT1.-, C5.-, C6.-
  N4: IC1.SDA_-_I2C_Data, R2.Pin_1, Atmega1.PC1
  N5: IC1.SCL_-_I2C_Clock, R1.Pin_1, Atmega1.PC0
  VDD: IC1.+V, R1.Pin_0, R2.Pin_0, U1.VDD, TFT1.MISO, Atmega1.VCC, Atmega1.AVCC, IC2.OUT, BATT1.NEG, C5.+
  N6: U1.CD_DAT3, Atmega1.PB0
  N7: U1.CMD, TFT1.D/C, Atmega1.PB5
  N8: U1.CLK, TFT1.RST, Atmega1.PB7
  N9: U1.DAT0, TFT1.VCC, Atmega1.PB6
  N10: TFT1.SCK, Atmega1.PD2
  N11: TFT1.MOSI, Atmega1.PD1
  N12: TFT1.CS, Atmega1.PB2
  N13: TFT1.SDCS, Atmega1.PB1
  N14: TFT1.GND, Atmega1.PB3
  N15: Atmega1.XTAL2, C2.0, XTAL1.pin_0
  N16: Atmega1.XTAL1, C4.0, XTAL1.pin_1
  N17: Atmega1.AREF, C3.0
  N18: Atmega1.PA6, KEYPAD1.7
  N19: Atmega1.PA5, KEYPAD1.6
  N20: Atmega1.PA4, KEYPAD1.5
  N21: Atmega1.PA3, KEYPAD1.4
  N22: Atmega1.PA2, KEYPAD1.3
  N23: Atmega1.PA1, KEYPAD1.2
  N24: Atmega1.PA0, KEYPAD1.1
  N25: IC2.IN, BATT1.POS, C6.+

custom parts:
  1.8" TFT Display with uSD: 1.8" TFT Display with SPI control and MicroSD card
  Membrane Matrix Keypad: Membrane Matrix 3x4 Keypad
  4xAA Switchable Battery Pack w/Bare Wire: 4xAA Switchable Battery Pack with Bare Wire connection
